// Logisim project ex4.circ as structural Verilog: 1 circuit, main circuit main
module main (
  input  in_1,
  input  in_2,
  input  in_3,
  input  in_4,
  input  in_5,
  input  in_6,
  output out_7,
  output out_8
);

  wire and_1_out, and_2_out, not_1_out, not_2_out, not_3_out, or_1_out;

  not not_1 (not_1_out, in_5);
  not not_2 (not_2_out, in_1);
  not not_3 (not_3_out, in_2);
  or or_1 (or_1_out, in_4, not_1_out);
  and and_1 (and_1_out, in_1, in_3);
  and and_2 (and_2_out, not_2_out, not_3_out, in_3);
  and and_3 (out_8, or_1_out, in_6);
  or or_2 (out_7, and_1_out, and_2_out);
endmodule
