// Logisim project ex5.circ as structural Verilog: 2 circuits, main circuit main
module main (
  input  [7:0] in_1,
  output [2:0] out_2,
  output [2:0] out_3
);

  wire demultiplexer_1_out1, demultiplexer_1_out2, demultiplexer_1_out3, demultiplexer_1_out4,
       demultiplexer_1_out5, demultiplexer_1_out6, demultiplexer_1_out7, not_1_out, not_2_out, not_3_out,
       not_4_out, not_5_out, not_6_out, not_7_out, not_8_out, not_9_out, not_10_out, not_11_out, not_12_out,
       not_13_out, not_14_out, not_15_out, not_16_out, not_17_out, not_18_out, not_19_out, or_1_out,
       or_2_out, or_3_out, or_4_out, or_5_out, or_6_out, tune1_1, tune2_1, tune3_1, tune4_1, tune5_1,
       tune6_1, tune7_1;
  wire [2:0] multiplexer_1_out, multiplexer_2_out, multiplexer_3_out, multiplexer_5_out, multiplexer_7_out,
       multiplexer_12_out, multiplexer_15_out, multiplexer_16_out, multiplexer_18_out, multiplexer_19_out;

  not not_1 (not_1_out, in_1[7]);
  Multiplexer #(.enable("false"), .width(3)) multiplexer_1 (
    .in0({3{in_1[7]}}), .in1({{2{in_1[6]}}, 1'b0}), .out(multiplexer_1_out), .sel(not_1_out));
  or or_1 (or_1_out, in_1[6], in_1[7]);
  not not_2 (not_2_out, or_1_out);
  Multiplexer #(.enable("false"), .width(3)) multiplexer_2 (
    .in0(multiplexer_1_out), .in1(multiplexer_3_out), .out(multiplexer_2_out), .sel(not_2_out));
  not not_3 (not_3_out, in_1[5]);
  Multiplexer #(.enable("false"), .width(3)) multiplexer_3 (
    .in0({in_1[5], 1'b0, in_1[5]}), .in1({in_1[4], 2'b00}), .out(multiplexer_3_out), .sel(not_3_out));
  or or_2 (or_2_out, in_1[4], in_1[5], in_1[6], in_1[7]);
  not not_4 (not_4_out, or_2_out);
  Multiplexer #(.enable("false"), .width(3)) multiplexer_4 (
    .in0(multiplexer_2_out), .in1(multiplexer_7_out), .out(out_2), .sel(not_4_out));
  not not_5 (not_5_out, in_1[3]);
  Multiplexer #(.enable("false"), .width(3)) multiplexer_5 (
    .in0({1'b0, {2{in_1[3]}}}), .in1({1'b0, in_1[2], 1'b0}), .out(multiplexer_5_out), .sel(not_5_out));
  or or_3 (or_3_out, in_1[2], in_1[3]);
  not not_6 (not_6_out, in_1[1]);
  Multiplexer #(.enable("false")) multiplexer_6 (
    .in0(in_1[1]), .in1(not_6_out), .out(tune1_1), .sel(demultiplexer_1_out1));
  not not_7 (not_7_out, or_3_out);
  Multiplexer #(.enable("false"), .width(3)) multiplexer_7 (
    .in0(multiplexer_5_out), .in1({2'b00, in_1[1]}), .out(multiplexer_7_out), .sel(not_7_out));
  not not_8 (not_8_out, in_1[2]);
  Multiplexer #(.enable("false")) multiplexer_8 (
    .in0(in_1[2]), .in1(not_8_out), .out(tune2_1), .sel(demultiplexer_1_out2));
  not not_9 (not_9_out, in_1[3]);
  Multiplexer #(.enable("false")) multiplexer_9 (
    .in0(in_1[3]), .in1(not_9_out), .out(tune3_1), .sel(demultiplexer_1_out3));
  not not_10 (not_10_out, in_1[4]);
  Multiplexer #(.enable("false")) multiplexer_10 (
    .in0(in_1[4]), .in1(not_10_out), .out(tune4_1), .sel(demultiplexer_1_out4));
  not not_11 (not_11_out, in_1[5]);
  Multiplexer #(.enable("false")) multiplexer_11 (
    .in0(in_1[5]), .in1(not_11_out), .out(tune5_1), .sel(demultiplexer_1_out5));
  not not_12 (not_12_out, tune7_1);
  Multiplexer #(.enable("false"), .width(3)) multiplexer_12 (
    .in0({3{tune7_1}}), .in1({{2{tune6_1}}, 1'b0}), .out(multiplexer_12_out), .sel(not_12_out));
  or or_4 (or_4_out, tune6_1, tune7_1);
  not not_13 (not_13_out, in_1[6]);
  Multiplexer #(.enable("false")) multiplexer_13 (
    .in0(in_1[6]), .in1(not_13_out), .out(tune6_1), .sel(demultiplexer_1_out6));
  not not_14 (not_14_out, or_4_out);
  Demultiplexer #(.enable("false"), .select(3)) demultiplexer_1 (
    .out1(demultiplexer_1_out1), .out2(demultiplexer_1_out2), .out3(demultiplexer_1_out3),
    .out4(demultiplexer_1_out4), .out5(demultiplexer_1_out5), .out6(demultiplexer_1_out6),
    .out7(demultiplexer_1_out7), .in(1'b1), .sel(out_2));  // open: out0
  not not_15 (not_15_out, in_1[7]);
  Multiplexer #(.enable("false")) multiplexer_14 (
    .in0(in_1[7]), .in1(not_15_out), .out(tune7_1), .sel(demultiplexer_1_out7));
  Multiplexer #(.enable("false"), .width(3)) multiplexer_15 (
    .in0(multiplexer_12_out), .in1(multiplexer_16_out), .out(multiplexer_15_out), .sel(not_14_out));
  not not_16 (not_16_out, tune5_1);
  Multiplexer #(.enable("false"), .width(3)) multiplexer_16 (
    .in0({tune5_1, 1'b0, tune5_1}), .in1({tune4_1, 2'b00}), .out(multiplexer_16_out), .sel(not_16_out));
  or or_5 (or_5_out, tune4_1, tune5_1, tune6_1, tune7_1);
  not not_17 (not_17_out, or_5_out);
  Multiplexer #(.enable("false"), .width(3)) multiplexer_17 (
    .in0(multiplexer_15_out), .in1(multiplexer_19_out), .out(out_3), .sel(not_17_out));
  not not_18 (not_18_out, tune3_1);
  or or_6 (or_6_out, tune2_1, tune3_1);
  Multiplexer #(.enable("false"), .width(3)) multiplexer_18 (
    .in0({1'b0, {2{tune3_1}}}), .in1({1'b0, tune2_1, 1'b0}), .out(multiplexer_18_out), .sel(not_18_out));
  not not_19 (not_19_out, or_6_out);
  Multiplexer #(.enable("false"), .width(3)) multiplexer_19 (
    .in0(multiplexer_18_out), .in1({2'b00, tune1_1}), .out(multiplexer_19_out), .sel(not_19_out));

  // Other names for the same wires on the sheet: tune1 = in_1[1]; tune0 = in_1[0]; tune2 = in_1[2]; tune3 = in_1[3];
  //   tune4 = in_1[4]; tune5 = in_1[5]; tune6 = in_1[6]; tune7 = in_1[7]
endmodule

module test (
  output [7:0] nomber,
  output [2:0] first_1,
  output [2:0] second_1
);

  wire clock_1_out;

  Clock clock_1 (.out(clock_1_out));
  AddMachine addmachine_1 (.clk(clock_1_out), .REG_OUT(nomber));  // open: ADD_OUT
  // main main_1: pin names not known; wires that end beside it: nomber, first_1, second_1
endmodule
